# Fritzing sketch wiring-diagram (saved by Fritzing 0.9.3b)
breadboards: 1

parts:
  MCU1 = Raspberry Pi Zero
  C1 = Electrolytic Capacitor [capacitance=1µF package="100 mil [THT, electrolytic]"]
  C2 = Electrolytic Capacitor [capacitance=1µF package="100 mil [THT, electrolytic]"]
  R1 = Photocell (LDR) [package=THT]
  R2 = Photocell (LDR) [package=THT]
  KY-1 = Keyes Relay [package=THT]

nets:
  N1: MCU1.pin_1, R1.pin_1, R2.pin_1
  N2: MCU1.pin_2, KY-1.power
  N3: MCU1.pin_6, MCU1.pin_9, MCU1.pin_14, C1.-, C2.-, KY-1.ground
  N4: MCU1.pin_7, KY-1.signal
  N5: MCU1.pin_11, C1.+, R1.pin_0
  N6: MCU1.pin_13, C2.+, R2.pin_0
  N7: KY-1.C, KY-1.NO

custom parts:
  Keyes Relay: The Keyes 5V relay module is suitable for SCM development, home appliance control. It uses a 5V~12V TIL control signal which can control DC / AC signal.
